# Fritzing sketch midi-io-breadboard (saved by Fritzing 0.9.2b)
breadboards: 1

parts:
  IC1 = IC, DIP package, 8 pins [chip_label=6N138 part_number=6N138]
  DIN1 = DIN-5 jack (MIDI) [package=THT]
  DIN2 = DIN-5 jack (MIDI) [package=THT]
  R1 = Resistor [tolerance=±5% resistance=220 power=220 package=THT]
  R2 = Resistor [tolerance=±5% resistance=220 package=THT]
  D2 = Diode [package=diode-1n4148]
  R3 = Resistor [tolerance=±5% resistance=220 package=THT]
  R4 = Resistor [tolerance=±5% resistance=4.7k package=THT]
  R5 = Resistor [tolerance=±5% resistance=220 package=THT]

nets:
  N1: IC1.pin2, D2.C, R3.Pin_1
  N2: IC1.pin3, DIN2.5
  N3: IC1.pin5, DIN1.2, R4.Pin_1
  N4: IC1.pin6, R5.Pin_1
  N5: IC1.pin7, R4.Pin_0
  N6: IC1.pin8, R1.Pin_1, R5.Pin_0
  N7: DIN1.5, R2.Pin_0
  N8: DIN1.4, R1.Pin_0
  N9: DIN2.4, R3.Pin_0

notes:
  UART TX
  UART RX
  MIDI Out
  MIDI In
  5V
  GND
